# Fritzing sketch findablock-breadboard (saved by Fritzing 0.9.2b)
breadboards: 1

parts:
  LED1 = LED - 5mm [color="Red (633nm)" package="5 mm [THT]"]
  J1 = Piezo Speaker
  R1 = Resistor [tolerance=±5% resistance=220 package="1206 [SMD]"]  # not connected
  Raspberry_Pi1 = Raspberry Pi B+

nets:
  N1: LED1.anode, Raspberry_Pi1.GPIO24
  N2: J1.pin1, Raspberry_Pi1.GPIO3, Raspberry_Pi1.GND
  N3: J1.pin2, Raspberry_Pi1.GPIO17
